// Logisim project cpu.circ as structural Verilog: 3 circuits, main circuit main
module main (
  input  [3:0] in_1,
  input  Reset,
  input  MemWrite,
  output [31:0] out_4,
  output [31:0] out_5
);

  wire CLK, not_1_out;

  alu ALU ();  // open: R, A, B, OP
  register_file REG_FILE ();  // open: CLR, CPSR_IN, WRN, CPSR_WE, RV2, RV1, WD, RD2, RD1, PC_IN, PC_WE, PC, CPSR, CLK
  ROM #(.addrWidth(4), .dataWidth(32)) rom_1 (.addr(in_1), .data(out_5), .sel(1'b1));
  Clock clock_1 (.out(CLK));
  RAM #(.addrWidth(4), .dataWidth(32)) ram_1 (
    .addr(in_1), .data(out_4), .sel(1'b1), .clk(CLK), .ld(not_1_out), .clr(Reset));
  not not_1 (not_1_out, MemWrite);
  assign out_4 = MemWrite ? out_5 : 32'bz;  // Controlled_Buffer controlled_buffer_1

  // Notes on the sheet:
  //   contents of rom_1 (hex, n*v repeats v):
  //   e3a01003 e3a02004 e0810002 eafffffe
  //   RD1
endmodule

module register_file (
  input  [3:0] RD2,
  input  CLR,
  input  [3:0] RD1,
  input  CLK,
  input  [31:0] WD,
  input  [31:0] CPSR_IN,
  input  [31:0] PC_IN,
  input  [3:0] WRN,
  input  CPSR_WE,
  input  PC_WE,
  output [31:0] PC,
  output [31:0] CPSR,
  output [31:0] RV2,
  output [31:0] RV1
);

  wire LR_WE, R0_WE, R1_WE, R2_WE, R3_WE, R4_WE, R5_WE, R6_WE, R7_WE, R8_WE, R9_WE, R10_WE, R11_WE, R12_WE,
       SP_WE;
  wire [31:0] LR_Q, PC_Q, R0_Q, R1_Q, R2_Q, R3_Q, R4_Q, R5_Q, R6_Q, R7_Q, R8_Q, R9_Q, R10_Q, R11_Q, R12_Q,
       SP_Q;

  Register #(.width(32), .trigger("falling")) register_1 (.D(WD), .en(R0_WE), .Q(R0_Q), .clk(CLK), .clr(CLR));
  Register #(.width(32), .trigger("falling")) register_2 (.D(WD), .en(R1_WE), .Q(R1_Q), .clk(CLK), .clr(CLR));
  Register #(.width(32), .trigger("falling")) register_3 (.D(WD), .en(R2_WE), .Q(R2_Q), .clk(CLK), .clr(CLR));
  Register #(.width(32), .trigger("falling")) register_4 (.D(WD), .en(R3_WE), .Q(R3_Q), .clk(CLK), .clr(CLR));
  Register #(.width(32), .trigger("falling")) register_5 (.D(WD), .en(R4_WE), .Q(R4_Q), .clk(CLK), .clr(CLR));
  Register #(.width(32), .trigger("falling")) register_6 (.D(WD), .en(R5_WE), .Q(R5_Q), .clk(CLK), .clr(CLR));
  Register #(.width(32), .trigger("falling")) register_7 (.D(WD), .en(R6_WE), .Q(R6_Q), .clk(CLK), .clr(CLR));
  Register #(.width(32), .trigger("falling")) register_8 (.D(WD), .en(R7_WE), .Q(R7_Q), .clk(CLK), .clr(CLR));
  Register #(.width(32), .trigger("falling")) register_9 (.D(WD), .en(R8_WE), .Q(R8_Q), .clk(CLK), .clr(CLR));
  Decoder #(.select(4), .enable("false")) decoder_1 (
    .out0(R0_WE), .out1(R1_WE), .out2(R2_WE), .out3(R3_WE), .out4(R4_WE), .out5(R5_WE), .out6(R6_WE),
    .out7(R7_WE), .out8(R8_WE), .out9(R9_WE), .out10(R10_WE), .out11(R11_WE), .out12(R12_WE), .out13(SP_WE),
    .out14(LR_WE), .sel(WRN));  // open: out15
  Register #(.width(32), .trigger("falling")) register_10 (.D(WD), .en(R9_WE), .Q(R9_Q), .clk(CLK), .clr(CLR));
  Register #(.width(32), .trigger("falling")) register_11 (.D(WD), .en(R10_WE), .Q(R10_Q), .clk(CLK), .clr(CLR));
  Register #(.width(32), .trigger("falling")) register_12 (.D(WD), .en(R11_WE), .Q(R11_Q), .clk(CLK), .clr(CLR));
  Register #(.width(32), .trigger("falling")) register_13 (.D(WD), .en(R12_WE), .Q(R12_Q), .clk(CLK), .clr(CLR));
  Register #(.width(32), .trigger("falling")) register_14 (.D(WD), .en(SP_WE), .Q(SP_Q), .clk(CLK), .clr(CLR));
  Register #(.width(32), .trigger("falling")) register_15 (.D(WD), .en(LR_WE), .Q(LR_Q), .clk(CLK), .clr(CLR));
  Register #(.width(32), .trigger("falling")) register_16 (.D(PC_IN), .en(PC_WE), .Q(PC), .clk(CLK), .clr(CLR));
  Register #(.width(32), .trigger("falling")) register_17 (.D(CPSR_IN), .en(CPSR_WE), .Q(CPSR), .clk(CLK), .clr(CLR));
  Multiplexer #(.select(4), .width(32), .enable("false")) multiplexer_1 (
    .in0(R0_Q), .in1(R1_Q), .in2(R2_Q), .in3(R3_Q), .in4(R4_Q), .in5(R5_Q), .in6(R6_Q), .in7(R7_Q),
    .in8(R8_Q), .in9(R9_Q), .in10(R10_Q), .in11(R11_Q), .in12(R12_Q), .in13(SP_Q), .in14(LR_Q), .in15(PC_Q),
    .out(RV2), .sel(RD2));
  Multiplexer #(.select(4), .width(32), .enable("false")) multiplexer_2 (
    .in0(R0_Q), .in1(R1_Q), .in2(R2_Q), .in3(R3_Q), .in4(R4_Q), .in5(R5_Q), .in6(R6_Q), .in7(R7_Q),
    .in8(R8_Q), .in9(R9_Q), .in10(R10_Q), .in11(R11_Q), .in12(R12_Q), .in13(SP_Q), .in14(LR_Q), .in15(PC_Q),
    .out(RV1), .sel(RD1));
endmodule

module alu (
  input  [1:0] OP,
  input  [31:0] A,
  input  [31:0] B,
  output [31:0] R
);

  wire [31:0] adder_1_out, multiplier_1_out, subtractor_1_out;

  Adder #(.width(32)) adder_1 (.a(A), .b(B), .out(adder_1_out));  // open: cin, cout
  Subtractor #(.width(32)) subtractor_1 (.a(A), .b(B), .out(subtractor_1_out));  // open: bin, bout
  Multiplier #(.width(32)) multiplier_1 (.a(A), .b(B), .out(multiplier_1_out));  // open: cin, cout
  Multiplexer #(.select(2), .width(32), .enable("false")) multiplexer_1 (
    .in0(adder_1_out), .in1(subtractor_1_out), .in2(multiplier_1_out), .out(R), .sel(OP));  // open: in3
endmodule
